# Fritzing sketch Lab1.1 (saved by Fritzing 0.9.4)
breadboards: 1

parts:
  U1 = 7400 4 x 2 Input NAND Gate [part_number=7400 package="DIP (Dual Inline) [THT]"]

nets:
  Input A: U1.A1
  Input B: Switch: U1.B1, U1.A4, U1.B4
  N1: U1.Q1, U1.Q2
  N2: U1.A2, U1.A3
  Output Z: U1.B2
  GND: U1.GND
  Input C: U1.B3
  N3: U1.Q3, U1.Q4
  3.3V: U1.VDD

notes:
  Output Z
  Input B: Switch
  Input A
  Input C
