# Fritzing sketch Lab1.2 (saved by Fritzing 0.9.4)
breadboards: 1

parts:
  U1 = 7400 4 x 2 Input NAND Gate [part_number=7400 package="DIP (Dual Inline) [THT]"]
  U2 = 7400 4 x 2 Input NAND Gate [part_number=7400 package="DIP (Dual Inline) [THT]"]

nets:
  Input A: U1.A1, U2.A4
  Input B: Switch: U1.B1, U1.A4, U1.B4
  N1: U1.Q1, U1.Q2
  N2: U1.A2, U1.A3
  N3: U1.B2, U2.A1, U2.B1
  GND: U1.GND, U2.GND
  Input C: U1.B3, U2.B4
  N4: U1.Q3, U1.Q4
  3.3V: U1.VDD, U2.VDD
  N5: U2.Q1, U2.Q2
  N6: U2.A2, U2.Q4
  Output Z: U2.B2

notes:
  Output Z
  Input B: Switch
  Input A
  Input C
