# Fritzing sketch Lab2.1 (saved by Fritzing 0.9.4)
breadboards: 3

parts:
  U1 = 7404 Hex Inverter [part_number=7404 package=dil14]
  U2 = 74151 8:1 MUX [part_number=74151 package="DIP16 [THT]"]
  U3 = 7402 4 x 2 Input NOR Gate [part_number=7402 package="DIP (Dual Inline) [THT]"]
  U4 = 7400 4 x 2 Input NAND Gate [part_number=7400 package="DIP (Dual Inline) [THT]"]
  U5 = 7486 4 x 2 Input XOR Gate [part_number=7486 package="DIP (Dual Inline) [THT]"]
  U6 = 74157 Quad 2:1 MUX [part_number=74157 package="DIP16 [THT]"]
  U7 = 74157 Quad 2:1 MUX [part_number=74157 package="DIP16 [THT]"]
  U8 = 74194 4 Bit Bi-Directional Shift Register [part_number=74194 package="DIP16 [THT]"]
  U9 = 74194 4 Bit Bi-Directional Shift Register [part_number=74194 package="DIP16 [THT]"]
  U10 = 74161 4 Bit Synchronous Up Down Counter [part_number=74161 package="DIP16 [THT]"]
  U11 = 7427 3 x 3 Input NOR Gate [part_number=7427 package="DIP (Dual Inline) [THT]"]
  U12 = 7404 Hex Inverter [part_number=7404 package=dil14]
  U14 = 7474 Dual Positive Edge Triggered D Flip Flop [part_number=7474 package="DIP (Dual Inline) [THT]"]
  U15 = 7400 4 x 2 Input NAND Gate [part_number=7400 package="DIP (Dual Inline) [THT]"]
  U16 = 7402 4 x 2 Input NOR Gate [part_number=7402 package="DIP (Dual Inline) [THT]"]
  U17 = 7404 Hex Inverter [part_number=7404 package=dil14]

nets:
  A NAND B: U1.1A, U2.15, U4.Q1
  A AND B: U1.1Y, U2.4
  A NOR B: U1.2A, U2.14, U3.Q1
  A OR B: U1.2Y, U2.3
  A XOR B: U1.3A, U2.2, U5.Q1
  A XNOR B: U1.3Y, U2.13
  GND: U1.GND, U2.7, U2.GND, U2.12, U3.GND, U4.GND, U5.GND, U6.!STROBE, U6.GND, U7.!STROBE, U7.GND, U8.GND, U9.GND, U10.3, U10.4, U10.7, U10.GND, U10.10, U11.GND, U12.GND, U14.GND, U15.GND, U16.GND, U17.GND
  3.3V: U1.VCC, U2.1, U2.VCC, U3.VDD, U4.VDD, U5.VDD, U6.VCC, U7.VCC, U8.1, U8.VCC, U9.1, U9.VCC, U10.1, U10.VCC, U11.VDD, U12.VCC, U14.A1, U14.Q2, U14.VDD, U15.VDD, U16.VDD, U17.VCC
  f (A, B): U2.5, U6.A1, U7.A1
  F2: U2.9
  F1: U2.10
  F0: U2.11
  Reg A: U3.A1, U4.A1, U5.A1, U6.A0, U6.B1, U8.12
  Reg B: U3.B1, U4.B1, U5.B1, U7.A0, U7.B1, U9.12
  N1: U6.B0, U7.Y1
  A*: U6.Y0, U8.7
  R1: U6.SEL
  N2: U6.Y1, U7.B0
  B*: U7.Y0, U9.7
  R0: U7.SEL
  D0: U8.3, U9.3
  D1: U8.4, U9.4
  D2: U8.5, U9.5
  D3: U8.6, U9.6
  N3: U8.9, U17.2Y
  LDA: U8.10, U16.A4
  CLK: U8.11, U9.11, U10.2, U14.Q1
  N4: U9.9, U17.1Y
  LDB: U9.10, U16.B3
  Shift: U10.9, U12.1Y, U16.A3, U16.Q4
  C1: U10.13, U11.B1, U11.Q2
  C0: U10.14, U11.A1, U11.Q1
  Execute: U11.A2, U15.A1
  NOT Q+: U11.B2, U14.B1
  NOT S: U11.A4, U12.1A
  E AND NOT Q: U11.B4, U12.2Y
  E NAND NOT Q: U12.2A, U15.Q1
  NOT Q: U14.A2, U15.B1
  Q: U14.B2
  N5: U16.Q3, U17.2A
  N6: U16.B4, U17.1A

notes:
  Computation Unit
  Routing Unit
  Register Unit
  Control Unit
  D3
  D2
  D1
  D0
  Execute
  LoadA
  LoadB
  A3-A0
  B3-B0

custom parts:
  7404 Hex Inverter: 74XX04 Hex Inverter, Modified by Zuofu Cheng (Aug 2020)
  74151 8:1 MUX: 74151 8:1 Multiplexor
  74157 Quad 2:1 MUX: 74157 Quad 2:1 Multiplexor
  7427 3 x 3 Input NOR Gate: 7427 3 x 2 Input NOR Gate
